# Fritzing sketch Iot System (saved by Fritzing 1.0.2b)
breadboards: 1

parts:
  A2 = Arduino Nano ESP32
  OLED_I2C1 = OLED 128x64 I2C Monochrome Display
  F1 = Fan - Ventilador [mn=30 package=THT]
  SHT35-D1 = SHT35-D [package="SIP (Single Inline) [THT]"]
  Q1 = NPN-Transistor [package="TO92 [THT]"]
  D1 = Diode [package=diode-1n4001]
  R1 = Resistor [tolerance=±5% resistance=220 package="2512 [SMD]"]

nets:
  VDD: A2.Pin_2, OLED_I2C1.VDD, SHT35-D1.VDD
  N1: A2.Pin_8, OLED_I2C1.SDA, SHT35-D1.SDA
  N2: A2.Pin_9, OLED_I2C1.SCK, SHT35-D1.SCL
  N3: A2.Pin_12, F1.5V, D1.C
  GND: A2.Pin_14, A2.Pin_19, OLED_I2C1.GND, SHT35-D1.GND, Q1.E
  N4: A2.Pin_22, R1.Pin_0
  N5: F1.GND, Q1.B, D1.A
  N6: Q1.C, R1.Pin_1

notes:
  5V Fan
  OLED Display
  SHT35 Sensor
  Ardunio Nano ESP32

custom parts:
  Arduino Nano ESP32: Arduino® Nano ESP32 tht.
  Fan - Ventilador: Ventilador de 2 pines, se encuentra comunmente en computadoras de escritorio
  SHT35-D: SHT35-D is an I2C connected temperature and humidity sensor
